// Logisim project Ex3.circ as structural Verilog: 1 circuit, main circuit main
module main (
  input  A,
  input  B,
  input  C,
  input  D,
  input  E,
  input  F,
  output out_7,
  output out_8,
  output out_9,
  output out_10,
  output out_11,
  output out_12
);

  A_main main_1 (.A(A), .B(B), .C(C), .D(D), .E(E), .F(F), .out_7(out_7));
  B_main main_2 (.A(A), .B(B), .C(C), .D(D), .E(E), .F(F), .out_7(out_8));
  C_main main_3 (.A(A), .B(B), .C(C), .D(D), .E(E), .F(F), .out_7(out_9));
  D_main main_4 (.A(A), .B(B), .C(C), .D(D), .E(E), .F(F), .out_7(out_10));
  E_main main_5 (.A(A), .B(B), .C(C), .D(D), .E(E), .F(F), .out_7(out_11));
  F_main main_6 (.A(A), .B(B), .C(C), .D(D), .E(E), .F(F), .out_7(out_12));
endmodule
